# Fritzing sketch peoplePlatine (saved by Fritzing 0.9.4)
circuit board: 11cm x 6.5cm
breadboards: 1

parts:
  MICRO = Arduino Micro (Rev3)
  S_RB = Camdenboss CTB0158-5 [part_number=CTB0158-5 package=THT]
  S_LF = Camdenboss CTB0158-5 [part_number=CTB0158-5 package=THT]
  S_LB = Camdenboss CTB0158-5 [part_number=CTB0158-5 package=THT]
  S_RF = Camdenboss CTB0158-5 [part_number=CTB0158-5 package=THT]
  C_RB_10 = Electrolytic Capacitor [capacitance=10µF package="100 mil [THT, electrolytic]"]
  C_RB_100 = Electrolytic Capacitor [capacitance=0.1mF package="100 mil [THT, electrolytic]"]
  C_LB_10 = Electrolytic Capacitor [capacitance=10µF package="100 mil [THT, electrolytic]"]
  C_RF_100 = Electrolytic Capacitor [capacitance=0.1mF package="100 mil [THT, electrolytic]"]
  C_LF_100 = Electrolytic Capacitor [capacitance=0.1mF package="100 mil [THT, electrolytic]"]
  C_RF_10 = Electrolytic Capacitor [capacitance=10µF package="100 mil [THT, electrolytic]"]
  C_LF_10 = Electrolytic Capacitor [capacitance=10µF package="100 mil [THT, electrolytic]"]
  PI = Raspberry Pi Zero
  R1 = Resistor [tolerance=±5% resistance=1k package=THT]
  R2 = Resistor [tolerance=±5% resistance=1k package=THT]
  R2_2 = Resistor [tolerance=±5% resistance=2.2k package=THT]
  R1_2 = Resistor [tolerance=±5% resistance=2.2k package=THT]
  C_LB_100 = Electrolytic Capacitor [capacitance=0.1mF package="100 mil [THT, electrolytic]"]
  Buzzer = Piezo Speaker
  R_LF = Resistor [tolerance=±5% resistance=220 package=THT]
  R_SL = Resistor [tolerance=±5% resistance=220 package=THT]
  R_LB = Resistor [tolerance=±5% resistance=220 package=THT]
  R_SR = Resistor [tolerance=±5% resistance=220 package=THT]
  R_RB = Resistor [tolerance=±5% resistance=220 package=THT]
  R_RF = Resistor [tolerance=±5% resistance=220 package=THT]
  Netzteil = Camdenboss CTB0158-2 [part_number=CTB0158-2 package=THT]
  Poti_Right = Rotary Potentiometer (Large) [maximum_resistance=100kΩ package=THT]
  Poti_Left = Rotary Potentiometer (Large) [maximum_resistance=100kΩ package=THT]
  LED_LB = LED - 5mm [color="Green (555nm)" package="5 mm [THT]"]
  LED_LF = LED - 5mm [color="Green (555nm)" package="5 mm [THT]"]
  LED_S_R = LED - 5mm [color="Yellow (585nm)" package="5 mm [THT]"]
  LED_RB = LED - 5mm [color="Green (555nm)" package="5 mm [THT]"]
  LED_RF = LED - 5mm [color="Green (555nm)" package="5 mm [THT]"]
  LED_S_L = LED - 5mm [color="Yellow (585nm)" package="5 mm [THT]"]

nets:
  N1: MICRO.RESET, PI.pin_22
  N2: MICRO.GND, S_RB.pin1, S_RB.pin4, S_LF.pin1, S_LF.pin4, S_LB.pin1, S_LB.pin4, S_RF.pin1, S_RF.pin4, C_RB_10.-, C_RB_100.-, C_LB_10.-, C_RF_100.-, C_LF_100.-, C_RF_10.-, C_LF_10.-, PI.pin_6, PI.pin_30, PI.pin_34, PI.pin_39, R2_2.Pin_1, R1_2.Pin_1, C_LB_100.-, Buzzer.pin1, Netzteil.pin2, Poti_Right.leg2, Poti_Left.leg2, LED_LB.cathode, LED_LF.cathode, LED_S_R.cathode, LED_RB.cathode, LED_RF.cathode, LED_S_L.cathode
  N3: MICRO.D2/SDA, R2.Pin_0
  N4: MICRO.D3/SCL, R1.Pin_0
  N5: MICRO.D4_PWM/A6, R_RF.Pin_1
  N6: MICRO.D5_PWM, R_RB.Pin_1
  N7: MICRO.D6_PWM/A7, R_SR.Pin_1
  N8: MICRO.D7, R_SL.Pin_1
  N9: MICRO.D8_PWM/A8, R_LF.Pin_1
  N10: MICRO.D9_PWM/A9, R_LB.Pin_1
  N11: MICRO.D10_PWM/A10, Buzzer.pin2
  N12: MICRO.5V, S_RB.pin2, S_RB.pin5, S_LF.pin2, S_LF.pin5, S_LB.pin2, S_LB.pin5, S_RF.pin2, S_RF.pin5, C_RB_10.+, C_RB_100.+, C_LB_10.+, C_RF_100.+, C_LF_100.+, C_RF_10.+, C_LF_10.+, PI.pin_4, C_LB_100.+, Netzteil.pin1, Poti_Right.leg1, Poti_Left.leg1
  N13: MICRO.A5, S_LF.pin3
  N14: MICRO.A4, S_LB.pin3
  N15: MICRO.A3, S_RF.pin3
  N16: MICRO.A2, S_RB.pin3
  N17: MICRO.A1, Poti_Left.wiper
  N18: MICRO.A0, Poti_Right.wiper
  N19: PI.pin_24, R1.Pin_1, R1_2.Pin_0
  N20: PI.pin_26, R2.Pin_1, R2_2.Pin_0
  N21: R_LF.Pin_0, LED_LF.anode
  N22: R_SL.Pin_0, LED_S_L.anode
  N23: R_LB.Pin_0, LED_LB.anode
  N24: R_SR.Pin_0, LED_S_R.anode
  N25: R_RB.Pin_0, LED_RB.anode
  N26: R_RF.Pin_0, LED_RF.anode
